# Fritzing sketch DomusSapiens (saved by Fritzing 0.9.3b)
breadboards: 1

parts:
  UNO = Arduino Uno (Rev3)
  ETHERNET = ENC28J60 [package=ssop28db]
  TX = RF-LINK_TX [package=rf-link_tx]
  RX = RF-LINK_RX [package=rf-link_rx]
  ANT = Antenna
  ANT_2 = Antenna
  R1 = Resistor [tolerance=±5% resistance=10k package=THT]
  LED1 = LED - 5mm [color="Blue (470nm)" package="5 mm [THT]"]
  Boost_converter = IC, DIP package, 4 pins [chip_label="Boost Converter"]
  DS1302 = IC, DIP package, 8 pins [chip_label=DS1302]
  XTAL1 = Crystal [frequency="32 kHz" package=THT]
  LED2 = LED - 5mm [color="Red (633nm)" package="5 mm [THT]"]

nets:
  N1: UNO.D8, DS1302.pin6
  N2: UNO.D9_PWM, DS1302.pin5
  N3: UNO.D10_PWM/SS, ETHERNET.CS
  N4: UNO.D11_PWM/MOSI, ETHERNET.SI
  N5: UNO.D12/MISO, ETHERNET.SO
  N6: UNO.D13/SCK, ETHERNET.SCK
  GND: UNO.GND, RX.GND, R1.Pin_0, Boost_converter.pin2, DS1302.pin4
  N7: UNO.D2, TX.DATA
  N8: UNO.D3_PWM, RX.DATA
  N9: UNO.D5_PWM, LED2.anode
  N10: UNO.D6_PWM, LED1.anode
  N11: UNO.D7, DS1302.pin7
  5V: UNO.5V, RX.+5V, Boost_converter.pin1, DS1302.pin1
  N12: TX.ANT, ANT.antenna_lead
  N13: TX.GND, Boost_converter.pin3
  N14: TX.+5V, Boost_converter.pin4
  N15: RX.ANT, ANT_2.antenna_lead
  N16: R1.Pin_1, LED1.cathode, LED2.cathode
  N17: DS1302.pin2, XTAL1.pin_1
  N18: DS1302.pin3, XTAL1.pin_0
