# Fritzing sketch DomusSapiensDevice (saved by Fritzing 0.9.3b)
breadboards: 1

parts:
  UNO = Arduino Uno (Rev3)
  Time = Trimmer Potentiometer [maximum_resistance=10kΩ package=THT]
  Relay_Down = RELAY [package=relay-g5q]
  Relay_Up = RELAY [package=relay-t9a]
  Switches = Header 3 [package=molex-1x3_lock]
  TX = RF-LINK_TX [package=rf-link_tx]
  RX = RF-LINK_RX [package=rf-link_rx]
  Pairing = Pushbutton [package="[THT]"]
  ANT = Antenna
  ANT_2 = Antenna
  Transformer = Transformer [package=transformer_smd]
  Mains = Header 3 [package=molex-1x3_lock]
  Boost_converter1 = IC, DIP package, 4 pins [chip_label="Boost Converter"]
  Motor = Header 4 [package=molex-1x4_lock]

nets:
  N1: UNO.A0, Time.wiper
  N2: UNO.D8, Switches.2
  GND: UNO.GND, Time.leg1, Relay_Down.COIL2, Relay_Up.COIL2, Switches.3, RX.GND, Pairing.Pin_1, Pairing.Pin_2, Transformer.1, Boost_converter1.pin2
  N3: UNO.D2, TX.DATA
  N4: UNO.D3_PWM, RX.DATA
  N5: UNO.D4, Pairing.Pin_4
  N6: UNO.D5_PWM, Relay_Up.COIL1
  N7: UNO.D6_PWM, Relay_Down.COIL1
  N8: UNO.D7, Switches.1
  5V: UNO.5V, Time.leg2, RX.+5V, Transformer.4, Boost_converter1.pin1
  N9: Relay_Down.MAIN, Relay_Up.MAIN, Transformer.2, Mains.2
  N10: Relay_Down.NO, Motor.3
  N11: Relay_Up.NO, Motor.2
  N12: TX.ANT, ANT.antenna_lead
  N13: TX.GND, Boost_converter1.pin3
  N14: TX.+5V, Boost_converter1.pin4
  N15: RX.ANT, ANT_2.antenna_lead
  N16: Transformer.3, Mains.1, Motor.1
  N17: Mains.3, Motor.4
